// Logisim project control_logic.circ as structural Verilog: 1 circuit, main circuit control_logic
module control_logic (
  input  [31:0] inst,
  input  BrEq,
  input  BrLt,
  output PCSel,
  output RegWEn,
  output [2:0] ImmSel,
  output BrUn,
  output ASel,
  output BSel,
  output [3:0] ALUSel,
  output MemRW,
  output [1:0] WBSel,
  output CSRSel,
  output CSRWen
);

  wire beq_out, bge_out, bgeu_out, blt_out, bltu_out, bne_out, comparator_1_eq, comparator_2_eq,
       comparator_3_eq, comparator_4_eq, comparator_5_eq, comparator_6_eq, comparator_17_eq,
       comparator_18_eq, comparator_19_eq, comparator_20_eq, comparator_21_eq, comparator_22_eq,
       comparator_23_eq, comparator_24_eq, comparator_25_eq, comparator_26_eq, comparator_27_eq,
       comparator_28_eq, comparator_29_eq, comparator_30_eq, comparator_31_eq, comparator_32_eq,
       comparator_33_eq, is_I_jalr, is_I_l, is_I_s, is_mul, is_mulh, is_R, is_SB, is_sra, is_srai, is_srl,
       is_srli, is_sub, is_U, is_U_auipc, is_U_lui, is_UJ, not_1_out, not_2_out, not_3_out, or_1_out,
       or_3_out, or_5_out, or_6_out, or_7_out, or_9_out, or_11_out;
  wire [1:0] multiplexer_6_out, multiplexer_7_out;
  wire [2:0] multiplexer_1_out, multiplexer_2_out, multiplexer_3_out, multiplexer_4_out;
  wire [3:0] multiplexer_9_out, multiplexer_10_out, multiplexer_11_out, multiplexer_12_out,
       multiplexer_13_out;

  Multiplexer #(.enable("false"), .width(3)) multiplexer_1 (
    .in0(3'b000), .in1(3'b001), .out(multiplexer_1_out), .sel(MemRW));
  Multiplexer #(.enable("false"), .width(3)) multiplexer_2 (
    .in0(multiplexer_1_out), .in1(3'b010), .out(multiplexer_2_out), .sel(is_SB));
  Multiplexer #(.enable("false"), .width(3)) multiplexer_3 (
    .in0(multiplexer_2_out), .in1(3'b011), .out(multiplexer_3_out), .sel(is_U));
  Multiplexer #(.enable("false"), .width(3)) multiplexer_4 (
    .in0(multiplexer_3_out), .in1(3'b100), .out(multiplexer_4_out), .sel(is_UJ));
  Comparator #(.width(3)) comparator_1 (.a(inst[14:12]), .b(3'b000), .eq(comparator_1_eq));  // open: gt, lt
  Comparator #(.width(3)) comparator_2 (.a(inst[14:12]), .b(3'b001), .eq(comparator_2_eq));  // open: gt, lt
  Comparator #(.width(3)) comparator_3 (.a(inst[14:12]), .b(3'b100), .eq(comparator_3_eq));  // open: gt, lt
  Comparator #(.width(3)) comparator_4 (.a(inst[14:12]), .b(3'b101), .eq(comparator_4_eq));  // open: gt, lt
  Comparator #(.width(3)) comparator_5 (.a(inst[14:12]), .b(3'b110), .eq(comparator_5_eq));  // open: gt, lt
  Comparator #(.width(3)) comparator_6 (.a(inst[14:12]), .b(3'b111), .eq(comparator_6_eq));  // open: gt, lt
  Multiplexer #(.enable("false"), .width(3)) multiplexer_5 (
    .in0(multiplexer_4_out), .in1(3'b101), .out(ImmSel), .sel(CSRWen));
  not not_1 (not_1_out, BrEq);
  not not_2 (not_2_out, BrLt);
  not not_3 (not_3_out, BrLt);
  and beq (beq_out, comparator_1_eq, BrEq, is_SB);
  and bne (bne_out, comparator_2_eq, not_1_out, is_SB);
  and blt (blt_out, comparator_3_eq, BrLt, is_SB);
  and bge (bge_out, comparator_4_eq, not_2_out, is_SB);
  and bltu (bltu_out, comparator_5_eq, BrLt, is_SB);
  and bgeu (bgeu_out, comparator_6_eq, not_3_out, is_SB);
  or or_1 (or_1_out, beq_out, bne_out, blt_out, bge_out, bltu_out, bgeu_out);
  Comparator #(.width(7)) comparator_7 (.a(inst[6:0]), .b(7'b0110011), .eq(is_R));  // open: gt, lt
  Comparator #(.width(7)) comparator_8 (.a(inst[6:0]), .b(7'b0000011), .eq(is_I_l));  // open: gt, lt
  Comparator #(.width(7)) comparator_9 (.a(inst[6:0]), .b(7'b0010011), .eq(is_I_s));  // open: gt, lt
  Comparator #(.width(7)) comparator_10 (.a(inst[6:0]), .b(7'b0100011), .eq(MemRW));  // open: gt, lt
  Comparator #(.width(7)) comparator_11 (.a(inst[6:0]), .b(7'b1100011), .eq(is_SB));  // open: gt, lt
  Comparator #(.width(7)) comparator_12 (.a(inst[6:0]), .b(7'b0010111), .eq(is_U_auipc));  // open: gt, lt
  Comparator #(.width(7)) comparator_13 (.a(inst[6:0]), .b(7'b0110111), .eq(is_U_lui));  // open: gt, lt
  Comparator #(.width(7)) comparator_14 (.a(inst[6:0]), .b(7'b1101111), .eq(is_UJ));  // open: gt, lt
  Comparator #(.width(7)) comparator_15 (.a(inst[6:0]), .b(7'b1100111), .eq(is_I_jalr));  // open: gt, lt
  Comparator #(.width(7)) comparator_16 (.a(inst[6:0]), .b(7'b1110011), .eq(CSRWen));  // open: gt, lt
  Comparator #(.width(3)) comparator_17 (.a(inst[14:12]), .b(3'b111), .eq(comparator_17_eq));  // open: gt, lt
  Comparator #(.width(3)) comparator_18 (.a(inst[14:12]), .b(3'b110), .eq(comparator_18_eq));  // open: gt, lt
  or or_2 (PCSel, or_1_out, or_3_out);
  or or_3 (or_3_out, is_UJ, is_I_jalr);
  or or_4 (RegWEn, is_R, is_I_l, is_I_s, is_U_auipc, is_U_lui, is_UJ, is_I_jalr);
  or or_5 (or_5_out, comparator_17_eq, comparator_18_eq);
  and and_1 (BrUn, or_5_out, is_SB);
  Comparator #(.width(3)) comparator_19 (.a(inst[14:12]), .b(3'b001), .eq(comparator_19_eq));  // open: gt, lt
  Comparator #(.width(7)) comparator_20 (.a(inst[31:25]), .b(7'b0000001), .eq(comparator_20_eq));  // open: gt, lt
  Comparator #(.width(3)) comparator_21 (.a(inst[14:12]), .b(3'b000), .eq(comparator_21_eq));  // open: gt, lt
  Comparator #(.width(7)) comparator_22 (.a(inst[31:25]), .b(7'b0000001), .eq(comparator_22_eq));  // open: gt, lt
  Comparator #(.width(3)) comparator_23 (.a(inst[14:12]), .b(3'b000), .eq(comparator_23_eq));  // open: gt, lt
  Comparator #(.width(7)) comparator_24 (.a(inst[31:25]), .b(7'b0100000), .eq(comparator_24_eq));  // open: gt, lt
  Multiplexer #(.enable("false"), .width(2)) multiplexer_6 (
    .in0(2'b00), .in1(2'b01), .out(multiplexer_6_out), .sel(or_6_out));
  or or_6 (or_6_out, is_R, is_U_auipc, is_I_s);
  Comparator #(.width(3)) comparator_25 (.a(inst[14:12]), .b(3'b101), .eq(comparator_25_eq));  // open: gt, lt
  Comparator #(.width(7)) comparator_26 (.a(inst[31:25]), .b({7{1'b0}}), .eq(comparator_26_eq));  // open: gt, lt
  Comparator #(.width(3)) comparator_27 (.a(inst[14:12]), .b(3'b101), .eq(comparator_27_eq));  // open: gt, lt
  Multiplexer #(.enable("false"), .width(2)) multiplexer_7 (
    .in0(multiplexer_6_out), .in1(2'b10), .out(multiplexer_7_out), .sel(or_7_out));
  or or_7 (or_7_out, is_I_jalr, is_UJ);
  and and_2 (is_mulh, comparator_19_eq, is_R, comparator_20_eq);
  and and_3 (is_mul, comparator_21_eq, is_R, comparator_22_eq);
  and and_4 (is_sub, comparator_23_eq, is_R, comparator_24_eq);
  and and_5 (is_srl, comparator_25_eq, is_R, comparator_26_eq);
  and and_6 (CSRSel, CSRWen, comparator_27_eq);
  Multiplexer #(.enable("false"), .width(2)) multiplexer_8 (
    .in0(multiplexer_7_out), .in1(2'b11), .out(WBSel), .sel(is_U_lui));
  or or_8 (ASel, is_UJ, is_U_auipc, is_SB);
  Multiplexer #(.enable("false"), .select(3), .width(4)) multiplexer_9 (
    .in0(4'b0000), .in1(4'b0110), .in2(4'b0111), .in3(4'b1011), .in4(4'b0011), .in5(4'b0100), .in6(4'b0010),
    .in7(4'b0001), .out(multiplexer_9_out), .sel(inst[14:12]));
  Multiplexer #(.enable("false"), .width(4)) multiplexer_10 (
    .in0(multiplexer_9_out), .in1(4'b1010), .out(multiplexer_10_out), .sel(is_mul));
  Comparator #(.width(3)) comparator_28 (.a(inst[14:12]), .b(3'b101), .eq(comparator_28_eq));  // open: gt, lt
  Comparator #(.width(7)) comparator_29 (.a(inst[31:25]), .b(7'b0100000), .eq(comparator_29_eq));  // open: gt, lt
  Comparator #(.width(3)) comparator_30 (.a(inst[14:12]), .b(3'b101), .eq(comparator_30_eq));  // open: gt, lt
  Comparator #(.width(7)) comparator_31 (.a(inst[31:25]), .b({7{1'b0}}), .eq(comparator_31_eq));  // open: gt, lt
  Comparator #(.width(3)) comparator_32 (.a(inst[14:12]), .b(3'b101), .eq(comparator_32_eq));  // open: gt, lt
  Comparator #(.width(7)) comparator_33 (.a(inst[31:25]), .b(7'b0100000), .eq(comparator_33_eq));  // open: gt, lt
  Multiplexer #(.enable("false"), .width(4)) multiplexer_11 (
    .in0(multiplexer_10_out), .in1(4'b1100), .out(multiplexer_11_out), .sel(is_sub));
  Multiplexer #(.enable("false"), .width(4)) multiplexer_12 (
    .in0(multiplexer_11_out), .in1(4'b1110), .out(multiplexer_12_out), .sel(is_mulh));
  or or_9 (or_9_out, is_sra, is_srai);
  and and_7 (is_sra, comparator_28_eq, is_R, comparator_29_eq);
  and and_8 (is_srli, comparator_30_eq, is_I_s, comparator_31_eq);
  and and_9 (is_srai, comparator_32_eq, is_I_s, comparator_33_eq);
  or or_10 (is_U, is_U_auipc, is_U_lui);
  Multiplexer #(.enable("false"), .width(4)) multiplexer_13 (
    .in0(multiplexer_12_out), .in1(4'b0101), .out(multiplexer_13_out), .sel(or_9_out));
  or or_11 (or_11_out, is_R, is_I_s);
  or or_12 (BSel, is_I_s, is_I_l, is_SB, is_I_jalr, is_U_auipc, is_U_lui, is_UJ);
  Multiplexer #(.enable("false"), .width(4)) multiplexer_14 (
    .in0(4'b0000), .in1(multiplexer_13_out), .out(ALUSel), .sel(or_11_out));

  // Other names for the same wires on the sheet: Ins6_0[6:0] = inst[6:0]; Opcode[6:0] = inst[6:0];
  //   Ins11_7[4:0] = inst[11:7]; rd[4:0] = inst[11:7]; funct3[2:0] = inst[14:12]; Ins14_12[2:0] = inst[14:12];
  //   Ins19_15[4:0] = inst[19:15]; rs1[4:0] = inst[19:15]; Ins24_20[4:0] = inst[24:20]; rs2[4:0] = inst[24:20];
  //   funct7[6:0] = inst[31:25]; Ins31_25[6:0] = inst[31:25]; is_csr = CSRWen; is_S = MemRW

  // Notes on the sheet:
  //   INPUTS to your circuit
  //   Inst 
  //   ImmSel
  //   0->I, 1->S, 2->SB, 3->U, 4->UJ, 5->csrwi
  //   PCSel
  //   DON'T CHANGE THE LOCATIONS OF THE INPUTS AND OUTPUTS!
  //   OUTPUT from your circuit
  //   RegWEn
  //   BrUn
  //   Categories
  //   sighed or unsigned
  //   2: slt7, slti7
  //   3: mulhu11
  //   6: or2, ori2
  //   0: add0, addi0, mul*10, sub*12
  //   1: sll6, slli6, mulh*14
  //   4: xor3, xori3
  //   5: srl4, srli4, sra*5, srai*5
  //   7: and1, andi1
  //   CSRSel and CSRWen
  //   WBSel
  //   0->load, 1->ALUout, 2->PC+4, 3->only_Imm
  //   funct3: Instruction ALUSel, so on...
  //   Some function cannot make clear only with funct3:
  //   A:1:PC,0:others
  //   AluSel
  //   ASel and BSel
  //   MemRW
  //   B:1:Imm_gen,0:rs2
endmodule
