// Logisim project cpu.circ as structural Verilog: 1 circuit, main circuit cpu
module cpu (
  input  clk,
  input  [31:0] INSTRUCTION,
  input  [31:0] READ_DATA,
  output [31:0] WRITE_ADDRESS,
  output [31:0] PROGRAM_COUNTER,
  output [31:0] ra,
  output [31:0] sp,
  output [31:0] t0,
  output [31:0] t1,
  output [31:0] t2,
  output [31:0] s0,
  output [31:0] s1,
  output [31:0] a0,
  output [31:0] tohost,
  output [3:0] WRITE_ENABLE,
  output [31:0] WRITE_DATA
);

  wire ASel, BrEq, BrLt, BrUn, BSel, comparator_1_eq, comparator_2_eq, comparator_3_eq, comparator_4_eq,
       comparator_5_eq, comparator_6_eq, comparator_7_eq, csr_1_p5, CSRSel, CSRWen, MemRW, PCSel, RegWEn;
  wire [1:0] WBSel;
  wire [2:0] funct3, ImmSel;
  wire [3:0] ALUSel, multiplexer_6_out, multiplexer_8_out, multiplexer_10_out;
  wire [4:0] Ins11_7, Ins19_15, Ins24_20;
  wire [6:0] Ins6_0, Ins31_25;
  wire [31:0] adder_2_out, ALU_Input_A, ALU_Input_B, imm, multiplexer_1_out, multiplexer_2_out,
       multiplexer_5_out, multiplexer_7_out, multiplexer_9_out, multiplexer_12_out, PC_4, PROGRAM_COUNTER_2,
       Read_1, READ_DATA_2, READ_DATA_b, READ_DATA_h, undriven, Write_Data_t;

  Multiplexer #(.enable("false"), .width(32)) multiplexer_1 (
    .in0(PC_4), .in1(WRITE_ADDRESS), .out(multiplexer_1_out), .sel(PCSel));
  Register #(.width(32)) PC (.D(multiplexer_1_out), .clk(clk), .Q(PROGRAM_COUNTER));  // open: en, clr
  Register #(.width(32)) register_1 (.D(PROGRAM_COUNTER), .clk(clk), .Q(PROGRAM_COUNTER_2));  // open: en, clr
  Register #(.width(32)) register_2 (
    .D(multiplexer_2_out), .clk(clk), .Q({Ins31_25, Ins24_20, Ins19_15, funct3, Ins11_7, Ins6_0}));  // open: en, clr
  Multiplexer #(.enable("false"), .width(32)) multiplexer_2 (
    .in0(INSTRUCTION), .in1(32'h13), .out(multiplexer_2_out), .sel(PCSel));
  Adder #(.width(32)) adder_1 (.a(32'h4), .b(PROGRAM_COUNTER), .out(PC_4));  // open: cin, cout
  control_logic control_logic_1 (
    .CSRWen(CSRWen), .PCSel(PCSel), .RegWEn(RegWEn), .ImmSel(ImmSel), .BrUn(BrUn), .ASel(ASel), .BSel(BSel),
    .ALUSel(ALUSel), .MemRW(MemRW), .WBSel(WBSel), .CSRSel(CSRSel),
    .inst({Ins31_25, Ins24_20, Ins19_15, funct3, Ins11_7, Ins6_0}), .BrEq(BrEq), .BrLt(BrLt));
  regfile regfile_1 (
    .rs1(Ins19_15), .rs2(Ins24_20), .rd(Ins11_7), .Write_Data(Write_Data_t), .RegWEn(RegWEn), .clk(clk),
    .ra(ra), .sp(sp), .t0(t0), .t1(t1), .t2(t2), .s0(s0), .s1(s1), .a0(a0), .Read_Data_1(Read_1),
    .Read_Data_2(WRITE_DATA));
  imm_gen imm_gen_1 (.inst({Ins31_25, Ins24_20, Ins19_15, funct3, Ins11_7, Ins6_0}), .ImmSel(ImmSel), .imm(imm));
  Multiplexer #(.enable("false"), .width(32)) multiplexer_3 (
    .in0(Read_1), .in1(PROGRAM_COUNTER_2), .out(ALU_Input_A), .sel(ASel));
  Multiplexer #(.enable("false"), .width(32)) multiplexer_4 (
    .in0(WRITE_DATA), .in1(imm), .out(ALU_Input_B), .sel(BSel));
  branch_comp branch_comp_1 (.rs1(Read_1), .rs2(WRITE_DATA), .BrUn(BrUn), .BrEq(BrEq), .BrLt(BrLt));
  Multiplexer #(.enable("false"), .width(32)) multiplexer_5 (
    .in0(Read_1), .in1(imm), .out(multiplexer_5_out), .sel(CSRSel));
  alu alu_1 (.Result(WRITE_ADDRESS), .A(ALU_Input_A), .B(ALU_Input_B), .ALUSel(ALUSel));
  // csr csr_1: pin names not known; wires that end beside it: 12'h51e, multiplexer_5_out, CSRWen, clk, csr_1_p5, tohost
  Comparator #(.width(3)) comparator_1 (.a(funct3), .b(3'b010), .eq(comparator_1_eq));  // open: gt, lt
  Multiplexer #(.enable("false"), .width(4)) multiplexer_6 (
    .in1(4'b1111), .out(multiplexer_6_out), .sel(comparator_2_eq));  // open: in0
  Comparator #(.width(3)) comparator_2 (.a(funct3), .b(3'b010), .eq(comparator_2_eq));  // open: gt, lt
  Multiplexer #(.enable("false"), .width(32)) multiplexer_7 (
    .in1(READ_DATA), .out(multiplexer_7_out), .sel(comparator_1_eq));  // open: in0
  Multiplexer #(.enable("false"), .width(4)) multiplexer_8 (
    .in0(multiplexer_6_out), .in1(4'b0011), .out(multiplexer_8_out), .sel(comparator_3_eq));
  Comparator #(.width(3)) comparator_3 (.a(funct3), .b(3'b001), .eq(comparator_3_eq));  // open: gt, lt
  Multiplexer #(.enable("false"), .width(32)) multiplexer_9 (
    .in0(multiplexer_7_out), .in1(READ_DATA_h), .out(multiplexer_9_out), .sel(comparator_4_eq));
  Comparator #(.width(3)) comparator_4 (.a(funct3), .b(3'b001), .eq(comparator_4_eq));  // open: gt, lt
  assign READ_DATA_h = {{16{READ_DATA[15]}}, READ_DATA[15:0]};  // Bit_Extender bit_extender_1
  assign READ_DATA_b = {{24{READ_DATA[7]}}, READ_DATA[7:0]};  // Bit_Extender bit_extender_2
  Adder #(.width(32)) adder_2 (.a(32'h4), .b(PROGRAM_COUNTER_2), .out(adder_2_out));  // open: cin, cout
  Multiplexer #(.enable("false"), .width(4)) multiplexer_10 (
    .in0(multiplexer_8_out), .in1(4'b0001), .out(multiplexer_10_out), .sel(comparator_5_eq));
  Comparator #(.width(3)) comparator_5 (.a(funct3), .b(3'b000), .eq(comparator_5_eq));  // open: gt, lt
  Multiplexer #(.enable("false"), .width(4)) multiplexer_11 (
    .in0(4'b0000), .in1(multiplexer_10_out), .out(WRITE_ENABLE), .sel(MemRW));
  Multiplexer #(.enable("false"), .width(32)) multiplexer_12 (
    .in0(multiplexer_9_out), .in1(READ_DATA_b), .out(multiplexer_12_out), .sel(comparator_6_eq));
  Comparator #(.width(3)) comparator_6 (.a(funct3), .b(3'b000), .eq(comparator_6_eq));  // open: gt, lt
  Comparator #(.width(7)) comparator_7 (.a(Ins6_0), .b(7'b0000011), .eq(comparator_7_eq));  // open: gt, lt
  Multiplexer #(.enable("false"), .select(2), .width(32)) multiplexer_13 (
    .in0(READ_DATA_2), .in1(WRITE_ADDRESS), .in2(adder_2_out), .in3(imm), .out(Write_Data_t), .sel(WBSel));
  Multiplexer #(.enable("false"), .width(32)) multiplexer_14 (
    .in0(undriven), .in1(multiplexer_12_out), .out(READ_DATA_2), .sel(comparator_7_eq));

  // Other names for the same wires on the sheet: ALU_Res[31:0] = WRITE_ADDRESS;
  //   INSTRUCTION_2[31:0] = {Ins31_25, Ins24_20, Ins19_15, funct3, Ins11_7, Ins6_0}; Opcode[6:0] = Ins6_0;
  //   rd[4:0] = Ins11_7; Ins14_12[2:0] = funct3; rs1[4:0] = Ins19_15; rs2[4:0] = Ins24_20; Read_2[31:0] = WRITE_DATA;
  //   READ_DATA_0_7[7:0] = READ_DATA[7:0]; READ_DATA_0_15[15:0] = READ_DATA[15:0]

  // Notes on the sheet:
  //   NOP:addi x0, x0, 0
  //   Output to IMEM
  //   PC
  //   Pipeline
  //   Inst
  //   IMEM (do **NOT** move this)
  //   Inputs from IMEM
  //   Regfile
  //   Imm_gen
  //   It is OK to move the PC, RegFile, ALU, MEM, Branch Comp, Imm Gen, and Control Logic to wherever is most convenient for you when constructing your CPU, and to delete this text
  //   Control
  //   Inputs/Outputs for testing. Do **NOT** move these.
  //   ASel BSel Branch
  //   Outputs To DMEM
  //   CSR
  //   DMEM (do **NOT** move this)
  //   Inputs From DMEM
  //   Alu
  //   eg.Write_En[3] 控制 最高字节 (Byte 3) 
  //   Store
  //   Write_En 是一个4位的信号，它的每一位分别对应控制上述4个字节是否要被写入
  //   0xf:0b1111->sw, 0x3:0b0011->sh, 0x1:0b0001->sb, 0x0:0b0000->no write
  //   Load
  //   Write
endmodule
