// Logisim project imm_gen.circ as structural Verilog: 1 circuit, main circuit imm_gen
module imm_gen (
  input  [31:0] inst,
  input  [2:0] ImmSel,
  output [31:0] imm
);

  wire [31:0] Imm_for_CSR, Imm_for_I, Imm_for_S, Imm_for_SB, Imm_for_UJ;

  assign Imm_for_I = {{20{inst[31]}}, inst[31:20]};  // Bit_Extender bit_extender_1
  assign Imm_for_S = {{20{inst[31]}}, {inst[31:25], inst[11:7]}};  // Bit_Extender bit_extender_2
  assign Imm_for_SB = {{19{inst[31]}}, {inst[31], inst[7], inst[30:25], inst[11:8], 1'b0}};  // Bit_Extender bit_extender_3
  assign Imm_for_UJ = {{11{inst[31]}}, {inst[31], inst[19:12], inst[20], inst[30:21], 1'b0}};  // Bit_Extender bit_extender_4
  assign Imm_for_CSR = {{27{1'b0}}, inst[19:15]};  // Bit_Extender bit_extender_5
  Multiplexer #(.enable("false"), .select(3), .width(32)) multiplexer_1 (
    .in0(Imm_for_I), .in1(Imm_for_S), .in2(Imm_for_SB), .in3({inst[31:12], {12{1'b0}}}), .in4(Imm_for_UJ),
    .in5(Imm_for_CSR), .out(imm), .sel(ImmSel));  // open: in6, in7

  // Other names for the same wires on the sheet: Ins11_7[4:0] = inst[11:7]; Ins11_8[3:0] = inst[11:8];
  //   rd[4:0] = inst[11:7]; Ins7 = inst[7]; Imm_for_U[31:12] = inst[31:12]; Ins21_30[9:0] = inst[30:21];
  //   Ins24_20[4:0] = inst[24:20]; Ins30_25[5:0] = inst[30:25]; Ins31_25[6:0] = inst[31:25]; Ins20 = inst[20];
  //   funct3[2:0] = inst[14:12]; Ins14_12[2:0] = inst[14:12]; Ins19_15[4:0] = inst[19:15]; rs1[4:0] = inst[19:15];
  //   Ins31 = inst[31]; laji = inst[31]; Ins6_0[6:0] = inst[6:0]; Opcode[6:0] = inst[6:0]

  // Notes on the sheet:
  //   INPUTS to your circuit
  //   DON'T CHANGE THE LOCATIONS OF THE INPUTS AND OUTPUTS!
  //   0->I, 1->S, 2->SB, 3->U, 4->UJ, 5->csrwi
  //   OUTPUT from your circuit
endmodule
